// Logisim project 8bitCPU.circ as structural Verilog
module ARITHMETIC_ADDER (
  input  [7:0] A,
  input  [7:0] B,
  input  Cin,
  output [7:0] SUM,
  output Cout
);

  wire adder_1_cout, adder_2_cout, adder_3_cout, adder_4_cout, adder_5_cout, adder_6_cout, adder_7_cout;

  Adder #(.width(1)) adder_1 (.a(A[0]), .b(B[0]), .out(SUM[0]), .cin(Cin), .cout(adder_1_cout));
  Adder #(.width(1)) adder_2 (.a(A[1]), .b(B[1]), .out(SUM[1]), .cin(adder_1_cout), .cout(adder_2_cout));
  Adder #(.width(1)) adder_3 (.a(A[2]), .b(B[2]), .out(SUM[2]), .cin(adder_2_cout), .cout(adder_3_cout));
  Adder #(.width(1)) adder_4 (.a(A[3]), .b(B[3]), .out(SUM[3]), .cin(adder_3_cout), .cout(adder_4_cout));
  Adder #(.width(1)) adder_5 (.a(A[4]), .b(B[4]), .out(SUM[4]), .cin(adder_4_cout), .cout(adder_5_cout));
  Adder #(.width(1)) adder_6 (.a(A[5]), .b(B[5]), .out(SUM[5]), .cin(adder_5_cout), .cout(adder_6_cout));
  Adder #(.width(1)) adder_7 (.a(A[6]), .b(B[6]), .out(SUM[6]), .cin(adder_6_cout), .cout(adder_7_cout));
  Adder #(.width(1)) adder_8 (.a(A[7]), .b(B[7]), .out(SUM[7]), .cin(adder_7_cout), .cout(Cout));
endmodule

module ADDER_SUBTRACTOR (
  input  [7:0] A,
  input  [7:0] B,
  input  Asen,
  output [7:0] SUM
);

  wire [7:0] multiplexer_1_out, not_1_out;

  assign not_1_out = ~B;  // NOT_Gate not_1, 8 bits wide
  Multiplexer #(.width(8)) multiplexer_1 (.in0(B), .in1(not_1_out), .out(multiplexer_1_out), .sel(Asen));  // open: en
  ARITHMETIC_ADDER arithmetic_adder_1 (.A(A), .B(multiplexer_1_out), .Cin(Asen), .SUM(SUM));  // open: Cout
endmodule

module REGISTERS (
  input  CLOCK,
  input  [7:0] Rin,
  input  RESET,
  input  [2:0] Rselect,
  input  [2:0] Rshow,
  output [7:0] R0_Q,
  output [7:0] R1_Q,
  output [7:0] R2_Q,
  output [7:0] R3_Q,
  output [7:0] R4_Q,
  output [7:0] R5_Q,
  output [7:0] R6_Q,
  output [7:0] R7_Q,
  output [7:0] Rinside
);

  wire decoder_1_out0, decoder_1_out1, decoder_1_out2, decoder_1_out3, decoder_1_out4, decoder_1_out5,
       decoder_1_out6, decoder_1_out7, not_1_out;

  Register R0 (.D(Rin), .en(decoder_1_out0), .Q(R0_Q), .clk(CLOCK), .clr(RESET));
  Register R1 (.D(Rin), .en(decoder_1_out1), .Q(R1_Q), .clk(CLOCK), .clr(RESET));
  Register R2 (.D(Rin), .en(decoder_1_out2), .Q(R2_Q), .clk(CLOCK), .clr(RESET));
  Register R3 (.D(Rin), .en(decoder_1_out3), .Q(R3_Q), .clk(CLOCK), .clr(RESET));
  Register R4 (.D(Rin), .en(decoder_1_out4), .Q(R4_Q), .clk(CLOCK), .clr(RESET));
  Register R5 (.D(Rin), .en(decoder_1_out5), .Q(R5_Q), .clk(CLOCK), .clr(RESET));
  Register R6 (.D(Rin), .en(decoder_1_out6), .Q(R6_Q), .clk(CLOCK), .clr(RESET));
  Register R7 (.D(Rin), .en(decoder_1_out7), .Q(R7_Q), .clk(CLOCK), .clr(RESET));
  Multiplexer #(.select(3), .width(8)) multiplexer_1 (
    .in0(R0_Q), .in1(R1_Q), .in2(R2_Q), .in3(R3_Q), .in4(R4_Q), .in5(R5_Q), .in6(R6_Q), .in7(R7_Q),
    .out(Rinside), .sel(Rshow));  // open: en
  not not_1 (not_1_out, RESET);
  Decoder #(.select(3)) decoder_1 (
    .out0(decoder_1_out0), .out1(decoder_1_out1), .out2(decoder_1_out2), .out3(decoder_1_out3),
    .out4(decoder_1_out4), .out5(decoder_1_out5), .out6(decoder_1_out6), .out7(decoder_1_out7),
    .sel(Rselect), .en(not_1_out));
endmodule

module ALU (
  input  [7:0] MUX,
  input  Ain,
  input  RESET,
  input  CLOCK,
  input  [7:0] MUX2,
  input  Asen,
  input  Bin,
  output [7:0] SUM
);

  wire [7:0] adder_subtractor_1_sum, RA_q;

  Register RA (.D(MUX), .en(Ain), .Q(RA_q), .clk(CLOCK), .clr(RESET));
  ADDER_SUBTRACTOR adder_subtractor_1 (.A(RA_q), .B(MUX2), .Asen(Asen), .SUM(adder_subtractor_1_sum));
  Register RB (.D(adder_subtractor_1_sum), .en(Bin), .Q(SUM), .clk(CLOCK), .clr(RESET));
endmodule

module CPU (
  input  RUN,
  input  [2:0] Select_to_See_Register,
  input  RESET,
  output DONE
);

  wire clock_1_out, control_logic_1_ain, control_logic_1_asen, control_logic_1_bin, control_logic_1_rxin,
       control_logic_1_rxout, control_logic_1_ryout;
  wire [1:0] control_logic_1_dinout;
  wire [2:0] control_logic_1_xx, control_logic_1_yy;
  wire [3:0] registers_1_rinside, registers_1_rinside_2;
  wire [7:0] alu_1_sum, counter_1_q, multiplexer_1_out, multiplexer_2_out, multiplexer_3_out,
       registers_1_r0_q, registers_1_r1_q, registers_1_r2_q, registers_1_r3_q, registers_1_r4_q,
       registers_1_r5_q, registers_1_r6_q, registers_1_r7_q, rom_1_data;

  Counter counter_1 (.count(RUN), .Q(counter_1_q), .clk(clock_1_out), .clr(RESET));  // open: load, D, carry
  ROM rom_1 (.addr(counter_1_q), .data(rom_1_data), .sel(RUN));
  Clock clock_1 (.out(clock_1_out));
  CONTROL_LOGIC control_logic_1 (
    .DIN(rom_1_data), .Rxin(control_logic_1_rxin), .YY(control_logic_1_yy), .Rxout(control_logic_1_rxout),
    .XX(control_logic_1_xx), .Ryout(control_logic_1_ryout), .Ain(control_logic_1_ain),
    .Bin(control_logic_1_bin), .Asen(control_logic_1_asen), .Dinout(control_logic_1_dinout[0]),
    .CLOCK(clock_1_out), .Bout(control_logic_1_dinout[1]), .RESET(RESET), .RUN(RUN), .DONE(DONE));
  Multiplexer #(.select(3), .width(8)) multiplexer_1 (
    .in0(registers_1_r0_q), .in1(registers_1_r1_q), .in2(registers_1_r2_q), .in3(registers_1_r3_q),
    .in4(registers_1_r4_q), .in5(registers_1_r5_q), .in6(registers_1_r6_q), .in7(registers_1_r7_q),
    .out(multiplexer_1_out), .sel(control_logic_1_yy), .en(control_logic_1_ryout));
  Multiplexer #(.select(2), .width(8)) multiplexer_2 (
    .in0(multiplexer_1_out), .in1(rom_1_data), .in2(alu_1_sum), .out(multiplexer_2_out),
    .sel(control_logic_1_dinout), .en(control_logic_1_rxin));  // open: in3
  REGISTERS registers_1 (
    .CLOCK(clock_1_out), .Rshow(Select_to_See_Register), .Rselect(control_logic_1_xx),
    .Rinside({registers_1_rinside_2, registers_1_rinside}), .R0_Q(registers_1_r0_q), .R1_Q(registers_1_r1_q),
    .R2_Q(registers_1_r2_q), .R3_Q(registers_1_r3_q), .R4_Q(registers_1_r4_q), .R5_Q(registers_1_r5_q),
    .R6_Q(registers_1_r6_q), .R7_Q(registers_1_r7_q), .RESET(RESET), .Rin(multiplexer_2_out));
  Multiplexer #(.select(3), .width(8)) multiplexer_3 (
    .in0(registers_1_r0_q), .in1(registers_1_r1_q), .in2(registers_1_r2_q), .in3(registers_1_r3_q),
    .in4(registers_1_r4_q), .in5(registers_1_r5_q), .in6(registers_1_r6_q), .in7(registers_1_r7_q),
    .out(multiplexer_3_out), .sel(control_logic_1_xx), .en(control_logic_1_rxout));
  ALU alu_1 (
    .Ain(control_logic_1_ain), .MUX2(multiplexer_1_out), .Bin(control_logic_1_bin),
    .Asen(control_logic_1_asen), .CLOCK(clock_1_out), .SUM(alu_1_sum), .MUX(multiplexer_3_out), .RESET(RESET));
  Hex_Digit_Display hex_digit_display_1 (.value(registers_1_rinside_2));  // open: dp
  Hex_Digit_Display hex_digit_display_2 (.value(registers_1_rinside));  // open: dp

  // Notes on the sheet:
  //   contents of rom_1 (hex, n*v repeats v):
  //   68 b8 35 35 68 6f 4*b5 4*ad 4*ee
endmodule

module CONTROL_LOGIC (
  input  CLOCK,
  input  [7:0] DIN,
  input  RUN,
  input  RESET,
  output Rxin,
  output Rxout,
  output Ryout,
  output DONE,
  output Ain,
  output Bin,
  output [2:0] YY,
  output [2:0] XX,
  output Asen,
  output Dinout,
  output Bout
);

  wire ADD, and_1_out, and_2_out, and_3_out, ck01_2_out, ck01_out, ck10_out, ck11_out, d_ff_1_qn, d_ff_2_qn,
       d_ff_3_q, LSB, MSB, MV, MVI, not_1_out, or_1_out, or_2_out, or_3_out, or_4_out, or_5_out, or_6_out,
       or_7_out, or_8_out, or_9_out, SUB;
  wire [7:6] IR_q;

  D_Flip_Flop d_ff_1 (.clk(CLOCK), .D(d_ff_1_qn), .Q(LSB), .Qn(d_ff_1_qn), .en(RUN), .reset(or_2_out));  // open: preset
  Register IR (.D(DIN), .en(RUN), .Q({IR_q, XX, YY}), .clk(CLOCK), .clr(RESET));
  D_Flip_Flop d_ff_2 (
    .clk(d_ff_1_qn), .D(d_ff_2_qn), .Q(MSB), .Qn(d_ff_2_qn), .en(RUN), .reset(or_2_out));  // open: preset
  and and_1 (and_1_out, Rxin, Dinout);
  and and_2 (and_2_out, Rxin, Ryout);
  and and_3 (and_3_out, Rxin, Bout);
  Decoder #(.select(2)) decoder_1 (.out0(MV), .out1(MVI), .out2(ADD), .out3(SUB), .sel(IR_q), .en(RUN));
  or or_1 (or_1_out, and_1_out, and_2_out, and_3_out);
  or or_2 (or_2_out, d_ff_3_q, RESET);
  D_Flip_Flop d_ff_3 (.clk(CLOCK), .D(or_1_out), .Q(d_ff_3_q), .reset(not_1_out));  // open: Qn, preset, en
  not not_1 (not_1_out, or_1_out);
  D_Flip_Flop d_ff_4 (.clk(CLOCK), .D(or_1_out), .Q(DONE));  // open: Qn, preset, en, reset
  or or_3 (or_3_out, MV, MVI);
  or or_4 (or_4_out, ADD, SUB);
  or or_5 (or_5_out, ADD, SUB);
  or or_6 (or_6_out, ADD, SUB);
  or or_7 (or_7_out, ADD, SUB);
  or or_8 (or_8_out, ADD, SUB);
  or or_9 (or_9_out, ADD, SUB);
  and ck01 (ck01_out, or_3_out, ~MSB, LSB);  // AND_Gate
  and ck10 (ck10_out, or_6_out, MSB, ~LSB);  // AND_Gate
  and ck01_2 (ck01_2_out, MV, ~MSB, LSB);  // AND_Gate
  and ck01_3 (Ain, or_7_out, ~MSB, LSB);  // AND_Gate
  and ck10_2 (Bin, or_8_out, MSB, ~LSB);  // AND_Gate
  and ck10_3 (Asen, SUB, MSB, ~LSB);  // AND_Gate
  and ck01_4 (Dinout, MVI, ~MSB, LSB);  // AND_Gate
  and ck11 (ck11_out, MSB, or_4_out, LSB);
  and ck01_5 (Rxout, or_5_out, ~MSB, LSB);  // AND_Gate
  and ck11_2 (Bout, MSB, or_9_out, LSB);
  or or_10 (Rxin, ck01_out, ck11_out);
  or or_11 (Ryout, ck10_out, ck01_2_out);

  // Notes on the sheet:
  //   COUNTER
endmodule
